# Fritzing sketch SolarSaver-veroboard (saved by Fritzing 0.9.2b)
circuit board: 8.46667cm x 5.64444cm
stripboards: 1

parts:
  J1 = Screw terminal - 2 pins [package=THT]
  Part1 = Arduino Uno (Rev3)
  R1 = Resistor [tolerance=±5% resistance=55k package=THT]
  R2 = Resistor [tolerance=±5% resistance=27k package=THT]
  K1 = Relay [part_number=FRS1B-S package=THT]
  R3 = Photocell (LDR) [package=THT]
  R4 = Resistor [tolerance=±5% resistance=4.7k package=THT]
  R5 = Resistor [tolerance=±5% resistance=220 package=THT]
  S1 = Pushbutton [package=THT]
  LED7 = LED - 5mm [color="Red (633nm)" package="5 mm [THT]"]
  R7 = Resistor [resistance=220 tolerance=±5% package=THT]

nets:
  N1: J1.pin1, Part1.GND, R2.Pin_0, K1.COIL1, R4.Pin_0, R5.Pin_0, LED7.cathode
  N2: J1.pin2, R1.Pin_0
  N3: Part1.A0, R3.pin_1, R4.Pin_1
  N4: Part1.A1, R1.Pin_1, R2.Pin_1
  N5: Part1.D12/MISO, R7.Pin_1
  N6: Part1.D2, R5.Pin_1, S1.leg1
  N7: Part1.D5_PWM, K1.C1
  N8: Part1.5V, K1.COIL2, R3.pin_0, S1.leg0
  N9: LED7.anode, R7.Pin_0

notes:
  -
  +
  12V sense
  5V
